// Logisim project 02.circ as structural Verilog: 1 circuit, main circuit main
module main (
  input  in_1,
  input  in_2,
  input  in_3,
  output out_4
);

  wire nand_1_out;

  nand nand_1 (nand_1_out, in_2, in_3);
  nand nand_2 (out_4, in_1, nand_1_out);
endmodule
