// Logisim project ALU.circ as structural Verilog: 1 circuit, main circuit main
module main (
  input  [7:0] a,
  input  [7:0] b,
  input  [1:0] alu_op,
  output [7:0] alu_out
);

  wire undriven_3;
  wire [1:0] undriven_4;
  wire [7:0] adder_1_out, bitwise_a_and_b_out, subtractor_1_out, undriven, undriven_2;

  Adder adder_1 (.a(undriven), .b(undriven_2), .out(adder_1_out));  // open: cin, cout
  assign bitwise_a_and_b_out = a & b;  // AND_Gate bitwise_a_and_b, 8 bits wide
  Subtractor subtractor_1 (.a(8'h1), .b(a), .out(subtractor_1_out), .bin(undriven_3));  // open: bout
  Multiplexer #(.select(2), .width(8)) multiplexer_1 (
    .in0(adder_1_out), .in2(bitwise_a_and_b_out), .out(alu_out), .sel(undriven_4));  // open: in1, in3, en
endmodule
