// Logisim project week 4 cpu - alu starter.circ as structural Verilog: 2 circuits, main circuit ALU
module ALU (
  input  [7:0] A,
  input  [7:0] B,
  input  [1:0] Operation,
  output [7:0] ALU_Out
);

  wire [7:0] adder_1_out, and_1_out, shifter_1_out, subtractor_1_out;

  Adder adder_1 (.a(A), .b(B), .out(adder_1_out));  // open: cin, cout
  assign and_1_out = A & B;  // AND_Gate and_1, 8 bits wide
  Subtractor subtractor_1 (.a(A), .b(8'h1), .out(subtractor_1_out));  // open: bin, bout
  Shifter shifter_1 (.in(A), .\dist (3'b001), .out(shifter_1_out));
  Multiplexer #(.select(2), .width(8)) multiplexer_1 (
    .in0(adder_1_out), .in1(and_1_out), .in2(subtractor_1_out), .in3(shifter_1_out), .out(ALU_Out),
    .sel(Operation));  // open: en
endmodule

module Main_CPU (
  input  [7:0] in_1
);

  wire clock_1_out;
  wire [1:0] rom_1_data;
  wire [3:0] counter_1_q;
  wire [7:0] alu_1_alu_out, register_1_q;

  Counter #(.width(4), .max('hf)) counter_1 (.Q(counter_1_q), .clk(clock_1_out));  // open: load, D, count, carry, clr
  Clock clock_1 (.out(clock_1_out));
  ROM #(.addrWidth(4), .dataWidth(2)) rom_1 (.addr(counter_1_q), .data(rom_1_data));  // open: sel
  ALU alu_1 (.A(register_1_q), .B(in_1), .Operation(rom_1_data), .ALU_Out(alu_1_alu_out));
  Register register_1 (.D(alu_1_alu_out), .en(1'b1), .Q(register_1_q), .clk(clock_1_out));  // open: clr

  // Notes on the sheet:
  //   contents of rom_1 (hex, n*v repeats v):
  //   0 2 0 1 3 2
endmodule
